# Fritzing sketch Circuit_R1 (saved by Fritzing 0.9.3b)
breadboards: 1

parts:
  GSM_SIM_GPSR_SMS_SIM900_SIM1 = SIM800L [part_number=SIM800L package=THT]
  M1 = RioRand LM2596 [part_number=LM2596]
  Part1 = Arduino Uno (Rev3) [part_number=UNO]
  R10 = Photocell (LDR) [part_number="Environment LDR" package=THT]
  R11 = Photocell (LDR) [part_number="Lamp LDR" package=THT]
  LED1 = LEDs [part_number=Lamp package=led10mm]
  R4 = Resistor [tolerance=±5% resistance=1k package=THT]
  R5 = Resistor [tolerance=±5% resistance=1k package=THT]
  R6 = Resistor [tolerance=±5% resistance=22k package=THT]
  R7 = Resistor [tolerance=±5% resistance=10k package=THT]
  R8 = Resistor [tolerance=±5% resistance=1k package=THT]
  U1 = LCD-16X2 [package=lcd-16x2]
  R9 = Resistor [tolerance=±5% resistance=1k package="0402 [SMD]"]
  VCC1 = Battery block 9V
  R2 = Resistor [tolerance=±5% resistance=10k package="0402 [SMD]"]
  R3 = Resistor [tolerance=±5% resistance=1k package="0402 [SMD]"]

nets:
  N1: GSM_SIM_GPSR_SMS_SIM900_SIM1.VDD, M1.Pin_3
  N2: GSM_SIM_GPSR_SMS_SIM900_SIM1.SIM_TXD, Part1.D11_PWM/MOSI
  N3: GSM_SIM_GPSR_SMS_SIM900_SIM1.SIM_RXD, R6.Pin_0, R7.Pin_0
  N4: GSM_SIM_GPSR_SMS_SIM900_SIM1.GND#5, M1.Pin_4
  N5: Part1.A0, R10.pin_1, R8.Pin_0
  N6: Part1.A1, R11.pin_1, R5.Pin_1
  N7: Part1.D10_PWM/SS, R7.Pin_1
  N8: Part1.D0/RX, U1.RS
  N9: Part1.D1/TX, U1.E
  N10: Part1.D3_PWM, U1.DB4
  N11: Part1.D4, U1.DB5
  N12: Part1.D5_PWM, U1.DB6
  N13: Part1.D6_PWM, U1.DB7
  5V: Part1.5V, R10.pin_0, R11.pin_0, R4.Pin_1, U1.VDD, R9.Pin_0, R3.Pin_1
  GND: Part1.GND, LED1.A, R5.Pin_0, R6.Pin_1, R8.Pin_1, U1.VSS, U1.R_W, U1.K, VCC1.-, R2.Pin_0
  N14: LED1.C, R4.Pin_0
  N15: U1.VO, R2.Pin_1, R3.Pin_0
