# Fritzing sketch Untitled Sketch (saved by Fritzing 0.9.3b)
breadboards: 1

parts:
  Part1 = Arduino Uno (Rev3) - ICSP
  R1 = Photocell (LDR) [part_number=LDR package=THT]
  R2 = Resistor [tolerance=±5% resistance=10k package="1206 [SMD]"]
  LED1 = LEDs [part_number=Lamp package=led10mm]
  R3 = Photocell (LDR) [part_number=LDR package=THT]
  R4 = Resistor [tolerance=±5% resistance=10k package="1206 [SMD]"]
  GSM_SIM_GPSR_SMS_SIM900_SIM1 = SIM800L [package=THT]

nets:
  N1: Part1.A0, R1.pin_1, R2.Pin_0
  N2: Part1.A1, R3.pin_0, R4.Pin_1
  GND: Part1.GND, R2.Pin_1, LED1.A, R4.Pin_0, GSM_SIM_GPSR_SMS_SIM900_SIM1.GND
  N3: Part1.D2, GSM_SIM_GPSR_SMS_SIM900_SIM1.SIM_RXD
  N4: Part1.D3_PWM, GSM_SIM_GPSR_SMS_SIM900_SIM1.SIM_TXD
  5V: Part1.5V, R1.pin_0, LED1.C, R3.pin_1, GSM_SIM_GPSR_SMS_SIM900_SIM1.VDD
